# Fritzing sketch Sleeping phases (saved by Fritzing 0.9.3b)
breadboards: 1

parts:
  Part1 = Arduino Uno (Rev3) - ICSP
  Part2 = Bluetooth HC-05 Macho  # not connected
  RHT1 = Humidity and Temperature Sensor RHT03
  R1 = Resistor [tolerance=±5% resistance=220 package="0402 [SMD]"]
  R2 = Resistor [tolerance=±5% resistance=220 package="0402 [SMD]"]
  R3 = PHOTOCELL [package=photocell-kit]
  Part3 = LilyPad Accelerometer ADXL335  # not connected
  LED1 = smd LED [color="Green (555nm)" package="1206 [SMD]"]  # not connected

nets:
  N1: Part1.A0, R2.Pin_0, R3.P$2
  5V: Part1.5V, RHT1.Vcc, R1.Pin_0, R3.P$1
  N2: Part1.D7, RHT1.Data-signal, R1.Pin_1
  N3: Part1.GND, RHT1.GND_2, R2.Pin_1
